# Fritzing sketch RPiClock_circuit (saved by Fritzing 0.9.2b)
breadboards: 1

parts:
  Raspberry_Pi1 = Raspberry Pi 2
  U1 = 74HC595 [package="DIP16 [THT]"]
  U2 = 74HC595 [package="DIP16 [THT]"]
  Power_5V = Power plug
  U5 = 74HC595 [package="DIP16 [THT]"]
  U6 = 74HC595 [package="DIP16 [THT]"]
  TD62084APG = TD62084APG [chip_label=IC package="DIP (Dual Inline) [THT]"]
  R1 = Resistor [tolerance=±5% resistance=100k package=THT]
  R2 = Resistor [tolerance=±5% resistance=100k package=THT]
  R3 = Resistor [tolerance=±5% resistance=100k package=THT]
  R4 = Resistor [tolerance=±5% resistance=100k package=THT]
  R5 = Resistor [tolerance=±5% resistance=100k package=THT]
  R6 = Resistor [tolerance=±5% resistance=100k package=THT]
  R7 = Resistor [tolerance=±5% resistance=100k package=THT]
  TD62084APG1 = TD62084APG [chip_label=IC package="DIP (Dual Inline) [THT]"]
  R9 = Resistor [tolerance=±5% resistance=120k package=THT]
  R10 = Resistor [tolerance=±5% resistance=120k package=THT]
  R11 = Resistor [tolerance=±5% resistance=120k package=THT]
  R12 = Resistor [tolerance=±5% resistance=120k package=THT]
  R13 = Resistor [tolerance=±5% resistance=120k package=THT]
  R14 = Resistor [tolerance=±5% resistance=120k package=THT]
  R16 = Resistor [tolerance=±5% resistance=120k package=THT]
  TD62084APG2 = TD62084APG [chip_label=IC package="DIP (Dual Inline) [THT]"]
  R17 = Resistor [tolerance=±5% resistance=120k package=THT]
  R18 = Resistor [tolerance=±5% resistance=120k package=THT]
  R19 = Resistor [tolerance=±5% resistance=120k package=THT]
  R20 = Resistor [tolerance=±5% resistance=120k package=THT]
  R21 = Resistor [tolerance=±5% resistance=120k package=THT]
  R22 = Resistor [tolerance=±5% resistance=120k package=THT]
  R23 = Resistor [tolerance=±5% resistance=120k package=THT]
  R24 = Resistor [tolerance=±5% resistance=120k package=THT]
  TD62084APG3 = TD62084APG [chip_label=IC package="DIP (Dual Inline) [THT]"]
  R25 = Resistor [tolerance=±5% resistance=120k package=THT]
  R26 = Resistor [tolerance=±5% resistance=120k package=THT]
  R27 = Resistor [tolerance=±5% resistance=120k package=THT]
  R28 = Resistor [tolerance=±5% resistance=120k package=THT]
  R30 = Resistor [tolerance=±5% resistance=120k package=THT]
  R31 = Resistor [tolerance=±5% resistance=120k package=THT]
  R33 = Resistor [tolerance=±5% resistance=100k package=THT]
  R34 = Resistor [tolerance=±5% resistance=120k package=THT]
  R35 = Resistor [tolerance=±5% resistance=120k package=THT]
  R36 = Resistor [tolerance=±5% resistance=120k package=THT]
  IV-9 = 7 Segment Display
  IV-9_2 = 7 Segment Display
  IV-9_3 = 7 Segment Display
  IV-9_4 = 7 Segment Display
  U4 = Voltage Regulator - 3.3V [package="TO220 [THT]"]

nets:
  VCC: Raspberry_Pi1.3v3, Raspberry_Pi1.3V3, U1.MR, U1.VCC, U2.MR, U2.VCC, U5.MR, U5.VCC, U6.MR, U6.VCC, U4.output_voltage
  N1: Raspberry_Pi1.GPIO10, U1.DS
  N2: Raspberry_Pi1.GPIO9, U1.ST_CP, U2.ST_CP, U5.ST_CP, U6.ST_CP
  N3: Raspberry_Pi1.GPIO11, U1.SH_CP, U2.SH_CP, U5.SH_CP, U6.SH_CP
  GND: Raspberry_Pi1.GND, U1.GND, U1.OE, U2.GND, U2.OE, Power_5V.GND, U5.GND, U5.OE, U6.GND, U6.OE, TD62084APG.GND, TD62084APG1.GND, TD62084APG2.GND, TD62084APG3.GND, U4.GND
  5V: Raspberry_Pi1.5V, Power_5V.VCC, U4.input_voltage
  N4: U1.Q1, R1.Pin_1
  N5: U1.Q2, R2.Pin_1
  N6: U1.Q3, R3.Pin_1
  N7: U1.Q4, R4.Pin_1
  N8: U1.Q5, R5.Pin_1
  N9: U1.Q6, R6.Pin_1
  N10: U1.Q7, R7.Pin_1
  N11: U1.Q7', U2.DS
  N12: U1.Q0, R33.Pin_1
  N13: U2.Q1, R11.Pin_1
  N14: U2.Q2, R12.Pin_1
  N15: U2.Q3, R10.Pin_1
  N16: U2.Q4, R16.Pin_1
  N17: U2.Q5, R13.Pin_1
  N18: U2.Q6, R9.Pin_1
  N19: U2.Q7, R14.Pin_1
  N20: U2.Q7', U5.DS
  N21: U2.Q0, R34.Pin_1
  N22: U5.Q1, R19.Pin_1
  N23: U5.Q2, R20.Pin_1
  N24: U5.Q3, R18.Pin_1
  N25: U5.Q4, R24.Pin_1
  N26: U5.Q5, R21.Pin_1
  N27: U5.Q6, R17.Pin_1
  N28: U5.Q7, R22.Pin_1
  N29: U5.Q7', U6.DS
  N30: U5.Q0, R23.Pin_1
  N31: U6.Q1, R27.Pin_1
  N32: U6.Q2, R28.Pin_1
  N33: U6.Q3, R26.Pin_1
  N34: U6.Q4, R25.Pin_1
  N35: U6.Q5, R30.Pin_1
  N36: U6.Q6, R35.Pin_1
  N37: U6.Q7, R36.Pin_1
  N38: U6.Q0, R31.Pin_1
  N39: TD62084APG.I1, R7.Pin_0
  N40: TD62084APG.I2, R6.Pin_0
  N41: TD62084APG.I3, R5.Pin_0
  N42: TD62084APG.I4, R4.Pin_0
  N43: TD62084APG.I5, R3.Pin_0
  N44: TD62084APG.I6, R2.Pin_0
  N45: TD62084APG.I7, R1.Pin_0
  N46: TD62084APG.I8, R33.Pin_0
  N47: TD62084APG.O8, IV-9.Segment_DP
  N48: TD62084APG.O7, IV-9.Segment_G
  N49: TD62084APG.O6, IV-9.Segment_F
  N50: TD62084APG.O5, IV-9.Segment_E
  N51: TD62084APG.O4, IV-9.Segment_D
  N52: TD62084APG.O3, IV-9.Segment_C
  N53: TD62084APG.O2, IV-9.Segment_B
  N54: TD62084APG.O1, IV-9.Segment_A
  N55: TD62084APG1.I1, R14.Pin_0
  N56: TD62084APG1.I2, R9.Pin_0
  N57: TD62084APG1.I3, R13.Pin_0
  N58: TD62084APG1.I4, R16.Pin_0
  N59: TD62084APG1.I5, R10.Pin_0
  N60: TD62084APG1.I6, R12.Pin_0
  N61: TD62084APG1.I7, R11.Pin_0
  N62: TD62084APG1.I8, R34.Pin_0
  N63: TD62084APG1.O8, IV-9_2.Segment_DP
  N64: TD62084APG1.O7, IV-9_2.Segment_G
  N65: TD62084APG1.O6, IV-9_2.Segment_F
  N66: TD62084APG1.O5, IV-9_2.Segment_E
  N67: TD62084APG1.O4, IV-9_2.Segment_D
  N68: TD62084APG1.O3, IV-9_2.Segment_C
  N69: TD62084APG1.O2, IV-9_2.Segment_B
  N70: TD62084APG1.O1, IV-9_2.Segment_A
  N71: TD62084APG2.I1, R22.Pin_0
  N72: TD62084APG2.I2, R17.Pin_0
  N73: TD62084APG2.I3, R21.Pin_0
  N74: TD62084APG2.I4, R24.Pin_0
  N75: TD62084APG2.I5, R18.Pin_0
  N76: TD62084APG2.I6, R20.Pin_0
  N77: TD62084APG2.I7, R19.Pin_0
  N78: TD62084APG2.I8, R23.Pin_0
  N79: TD62084APG2.O8, IV-9_3.Segment_DP
  N80: TD62084APG2.O7, IV-9_3.Segment_G
  N81: TD62084APG2.O6, IV-9_3.Segment_F
  N82: TD62084APG2.O5, IV-9_3.Segment_E
  N83: TD62084APG2.O4, IV-9_3.Segment_D
  N84: TD62084APG2.O3, IV-9_3.Segment_C
  N85: TD62084APG2.O2, IV-9_3.Segment_B
  N86: TD62084APG2.O1, IV-9_3.Segment_A
  N87: TD62084APG3.I1, R36.Pin_0
  N88: TD62084APG3.I2, R35.Pin_0
  N89: TD62084APG3.I3, R30.Pin_0
  N90: TD62084APG3.I4, R25.Pin_0
  N91: TD62084APG3.I5, R26.Pin_0
  N92: TD62084APG3.I6, R28.Pin_0
  N93: TD62084APG3.I7, R27.Pin_0
  N94: TD62084APG3.I8, R31.Pin_0
  N95: TD62084APG3.O8, IV-9_4.Segment_DP
  N96: TD62084APG3.O7, IV-9_4.Segment_G
  N97: TD62084APG3.O6, IV-9_4.Segment_F
  N98: TD62084APG3.O5, IV-9_4.Segment_E
  N99: TD62084APG3.O4, IV-9_4.Segment_D
  N100: TD62084APG3.O3, IV-9_4.Segment_C
  N101: TD62084APG3.O2, IV-9_4.Segment_B
  N102: TD62084APG3.O1, IV-9_4.Segment_A
  3.3V: IV-9.common_anode, IV-9_2.common_anode, IV-9_3.common_anode, IV-9_4.common_anode

custom parts:
  TD62084APG: A DIP stand-in part for whatever IC you want. With 18 pins on a 900mil dual inline package (DIP) footprint.
